# Fritzing sketch Knock Detector (saved by Fritzing 0.7.10b)
breadboards: 1

parts:
  Arduino1 = Arduino
  J1 = Piezo Speaker
  R1 = Resistor [tolerance=±5% resistance=1M package=THT]
  R3 = Resistor [tolerance=±5% resistance=220 package=THT]
  R4 = Resistor [tolerance=±5% resistance=220 package=THT]
  R2 = Resistor [tolerance=±5% resistance=220 package=THT]
  LED1 = RGB LED - (4 legs) [package="5 mm [THT]"]

nets (from the breadboard view):
  N1: Arduino1.GND, J1.pin2, R1.Pin_0
  N2: Arduino1.D6, R4.Pin_0
  N3: Arduino1.D5, LED1.common_anode
  N4: Arduino1.D3, R2.Pin_0
  N5: Arduino1.+5V, R3.Pin_0
  N6: Arduino1.A0, J1.pin1, R1.Pin_1
  N7: R3.Pin_1, LED1.green_cathode
  N8: R4.Pin_1, LED1.blue_cathode
  N9: R2.Pin_1, LED1.red_cathode
